# Fritzing sketch Main Circuit (saved by Fritzing 1.0.0d)
breadboards: 1

parts:
  Part1 = Arduino Mega 2560 (Rev3)
  U1 = RFID RC522 SIP - 8 pins [chip_label="RFID RC522" package="SIP (Single Inline) [THT]"]
  U2 = ESP8266-01S [part_number=ESP8266]
  R1 = Photocell (LDR) [package=THT]
  OLED_I2C1 = OLED 128x64 I2C Monochrome Display
  J1 = Piezo Speaker
  DHT11_1 = DHT11 module
  J2 = Screw terminal - 2 pins [package=THT]
  M1 = DC Motor [voltage_(max)=6V voltage_(min)=3V]
  LED1 = LEDs [package=led10mm]
  Sensore_PIR_HC-SR502 = HC-SR501 Body Sensor Module

nets:
  N1: Part1.A1, DHT11_1.DATA
  N2: Part1.A4, OLED_I2C1.SDA
  N3: Part1.A5, OLED_I2C1.SCK
  N4: Part1.D15/RX3, J2.pin2
  N5: Part1.D14/TX3, J2.pin1
  VCC: Part1.5V, U1.VCC, U2.VCC, U2.CH_PD, OLED_I2C1.VDD, DHT11_1.VCC, Sensore_PIR_HC-SR502.VCC
  GND: Part1.GND, U1.GND, U2.GPIO_0, U2.GND, R1.pin_1, OLED_I2C1.GND, J1.pin1, DHT11_1.GND, M1.pin_2, LED1.A, Sensore_PIR_HC-SR502.GND
  N6: Part1.D0_RX0, U2.RXD
  N7: Part1.D1_TX0, U2.TXD
  N8: Part1.D3_PWM, J1.pin2
  N9: Part1.D4_PWM, R1.pin_0
  N10: Part1.D5_PWM, U1.RST
  N11: Part1.D39, Sensore_PIR_HC-SR502.OUT
  N12: Part1.D41, LED1.C
  N13: Part1.D43, M1.pin_1
  N14: Part1.D50, U1.MISO
  N15: Part1.D51, U1.MOSI
  N16: Part1.D52, U1.SCK
  N17: Part1.D53, U1.NSS

notes:
  To Pro Mini

custom parts:
  RFID RC522 SIP - 8 pins: A SIP stand-in part for RFID RC522 . With 8 pins on a 300 mil single inline package (SIP) footprint.
  DHT11 module: https://cdn-learn.adafruit.com/downloads/pdf/dht.pdf DHT11 black pcb module reference by:https://github.com/adafruit/Fritzing-Library/blob/master/parts/DHT11%20Humitidy%20and%20Temperature%20Sensor.fzpz
  HC-SR501 Body Sensor Module: Pyroelectric Infrared PIR Motion Sensor Detector Module
