# Fritzing sketch Mini Circuit (saved by Fritzing 1.0.0d)
circuit board: 8.47cm x 5.64444cm
breadboards: 1

parts:
  Arduino_Pro_Mini = Arduino Pro Mini v13
  Soil_Sensor = Soil Moisture Sensor
  Relay_Module = KY-019 5V Relay Module [package="Breakout board"]
  To_Mega = Screw terminal - 2 pins [package=THT]
  Power_IN = Screw terminal - 2 pins [package=THT]

nets:
  VCC: Arduino_Pro_Mini.VCC, Soil_Sensor.VCC, Relay_Module.+, Power_IN.pin2
  GND: Arduino_Pro_Mini.GND, Soil_Sensor.GND, Relay_Module.-, Power_IN.pin1
  N1: Arduino_Pro_Mini.D5_PWM, Soil_Sensor.SIG
  N2: Arduino_Pro_Mini.D3_PWM, Relay_Module.S
  N3: Arduino_Pro_Mini.D1/RX, To_Mega.pin1
  N4: Arduino_Pro_Mini.D0/TX, To_Mega.pin2

notes:
  by Project Group 4.1.9

custom parts:
  KY-019 5V Relay Module: KY-019 5V Relay module, used to control AC circuits. (Special thanks to vanepp for fixing the PCB holes and other errors)
